// Logisim project ALU.circ as structural Verilog: 3 circuits, main circuit main
module main (
  input  C0,
  input  Enable,
  input  [7:0] Constant,
  input  [2:0] Select_ALU,
  input  [7:0] IPA,
  input  [7:0] IPB,
  output Carry,
  output [7:0] \output ,
  output Borrow,
  output [7:0] mul_carry
);

  wire [7:0] not_1_out, op0, op1, op2, op3, op4, op5, Tmp1;

  Multiplier multiplier_1 (.a(IPA), .b(IPB), .out(op2), .cout(mul_carry));  // open: cin
  assign op4 = IPA | IPB;  // OR_Gate or_1, 8 bits wide
  assign op3 = IPA & IPB;  // AND_Gate and_1, 8 bits wide
  assign op5 = IPA ^ IPB;  // XOR_Gate xor_1, 8 bits wide
  assign not_1_out = ~IPB;  // NOT_Gate not_1, 8 bits wide
  Add_block add_block_1 (.C0(C0), .IPA(IPA), .IPB(IPB), .F_Carry(Carry), .OP(op0));
  Add_block add_block_2 (.C0(C0), .IPA(not_1_out), .IPB(Constant), .OP(Tmp1));  // open: F_Carry
  Add_block add_block_3 (.C0(C0), .IPA(IPA), .IPB(Tmp1), .F_Carry(Borrow), .OP(op1));
  Multiplexer #(.select(3), .width(8)) multiplexer_1 (
    .in0(op0), .in1(op1), .in2(op2), .in3(op3), .in4(op4), .in5(op5), .out(\output ), .sel(Select_ALU),
    .en(Enable));  // open: in6, in7

  // Other names for the same wires on the sheet: A0 = IPA[0]; InputA[7:0] = IPA; A1 = IPA[1]; A2 = IPA[2];
  //   A3 = IPA[3]; A4 = IPA[4]; A5 = IPA[5]; A6 = IPA[6]; A7 = IPA[7]; B0 = IPB[0]; InputB[7:0] = IPB; B1 = IPB[1];
  //   B2 = IPB[2]; B3 = IPB[3]; B4 = IPB[4]; B5 = IPB[5]; B6 = IPB[6]; B7 = IPB[7]; Select[2:0] = Select_ALU
endmodule

// ADD
module Add_block (
  input  C0,
  input  [7:0] IPA,
  input  [7:0] IPB,
  output F_Carry,
  output [7:0] OP
);

  wire adder_2_cout, adder_3_cout, adder_4_cout, adder_5_cout, adder_6_cout, adder_7_cout, adder_8_cout;

  Adder #(.width(1)) adder_1 (.a(IPA[7]), .b(IPB[7]), .out(OP[7]), .cin(adder_2_cout), .cout(F_Carry));
  Adder #(.width(1)) adder_2 (.a(IPA[6]), .b(IPB[6]), .out(OP[6]), .cin(adder_3_cout), .cout(adder_2_cout));
  Adder #(.width(1)) adder_3 (.a(IPA[5]), .b(IPB[5]), .out(OP[5]), .cin(adder_4_cout), .cout(adder_3_cout));
  Adder #(.width(1)) adder_4 (.a(IPA[4]), .b(IPB[4]), .out(OP[4]), .cin(adder_5_cout), .cout(adder_4_cout));
  Adder #(.width(1)) adder_5 (.a(IPA[3]), .b(IPB[3]), .out(OP[3]), .cin(adder_6_cout), .cout(adder_5_cout));
  Adder #(.width(1)) adder_6 (.a(IPA[2]), .b(IPB[2]), .out(OP[2]), .cin(adder_7_cout), .cout(adder_6_cout));
  Adder #(.width(1)) adder_7 (.a(IPA[1]), .b(IPB[1]), .out(OP[1]), .cin(adder_8_cout), .cout(adder_7_cout));
  Adder #(.width(1)) adder_8 (.a(IPA[0]), .b(IPB[0]), .out(OP[0]), .cin(C0), .cout(adder_8_cout));

  // Other names for the same wires on the sheet: A0 = IPA[0]; A1 = IPA[1]; A2 = IPA[2]; A3 = IPA[3]; A4 = IPA[4];
  //   A5 = IPA[5]; A6 = IPA[6]; A7 = IPA[7]; B0 = IPB[0]; B1 = IPB[1]; B2 = IPB[2]; B3 = IPB[3]; B4 = IPB[4];
  //   B5 = IPB[5]; B6 = IPB[6]; B7 = IPB[7]
endmodule

// ALU
module Some (
);

  main main_1 ();  // open: C0, Constant, IPA, IPB, Carry, output, Enable, Select_ALU, Borrow, mul_carry
endmodule
