// Logisim project PC_first.circ as structural Verilog: 1 circuit, main circuit main
module main (
  input  in_1,
  input  in_2,
  input  [7:0] in_3,
  input  in_4,
  input  in_5,
  input  in_6,
  input  [7:0] in_7,
  input  in_8,
  input  in_9,
  input  in_10,
  output [7:0] out_11
);

  wire clock;
  wire [0:0] ram_1_data;
  wire [6:0] offset;
  wire [7:0] adder_1_out, multiplexer_1_out, multiplexer_2_out, undriven;

  Multiplexer #(.width(8), .enable("false")) multiplexer_1 (
    .in0(adder_1_out), .in1(in_3), .out(multiplexer_1_out), .sel(in_6));
  Register IR (.D(undriven), .en(1'b1), .clk(clock), .clr(in_1));  // open: Q
  Register register_1 (.D(multiplexer_1_out), .en(1'b1), .Q(out_11), .clk(clock), .clr(in_10));
  Multiplexer #(.width(8)) multiplexer_2 (
    .in0(in_7), .in1({in_2, offset}), .out(multiplexer_2_out), .sel(ram_1_data[0]), .en(1'b1));
  Adder adder_1 (.a(multiplexer_2_out), .b(out_11), .out(adder_1_out), .cin(in_4));  // open: cout
  Register MAR (.en(1'b1), .clk(clock), .clr(in_8));  // open: D, Q
  RAM ram_1 (.addr(out_11), .data({offset, ram_1_data[0]}), .sel(1'b1), .clk(clock), .ld(in_9), .clr(in_5));
  Clock clock_1 (.out(clock));
  Hex_Digit_Display hex_digit_display_1 (.value(out_11[7:4]), .dp(1'b1));
  Hex_Digit_Display hex_digit_display_2 (.value(out_11[3:0]), .dp(1'b1));
  Hex_Digit_Display hex_digit_display_3 (.value(offset[6:3]), .dp(1'b1));
  Hex_Digit_Display hex_digit_display_4 (.value({offset[2:0], ram_1_data[0]}), .dp(1'b1));

  // Other names for the same wires on the sheet: a1[7:0] = in_7
endmodule
