// Logisim project PIPO.circ as structural Verilog
module PIPO (
  input  [1:0] in_1,
  input  in_2,
  input  in_3,
  input  in_4,
  input  in_5,
  input  in_6,
  input  in_7,
  input  in_8,
  input  in_9,
  input  in_10,
  input  in_11,
  input  in_12,
  input  in_13,
  output out_14,
  output OP_0,
  output out_16,
  output out_17,
  output out_18,
  output out_19,
  output out_20,
  output out_21
);

  wire clock_1_out, multiplexer_1_out, multiplexer_2_out, multiplexer_3_out, multiplexer_4_out,
       multiplexer_5_out, multiplexer_6_out, multiplexer_7_out, multiplexer_8_out;

  Clock clock_1 (.out(clock_1_out));
  Multiplexer #(.select(2)) multiplexer_1 (
    .in0(OP_0), .in1(in_10), .in2(out_16), .in3(in_11), .out(multiplexer_1_out), .sel(in_1));  // open: en
  D_Flip_Flop d_ff_1 (.clk(clock_1_out), .D(multiplexer_1_out), .Q(OP_0), .reset(in_12));  // open: Qn, preset, en
  D_Flip_Flop d_ff_2 (.clk(clock_1_out), .D(multiplexer_2_out), .Q(out_16), .reset(in_12));  // open: Qn, preset, en
  Multiplexer #(.select(2)) multiplexer_2 (
    .in0(out_16), .in1(OP_0), .in2(out_17), .in3(in_3), .out(multiplexer_2_out), .sel(in_1), .en(in_13));
  Multiplexer #(.select(2)) multiplexer_3 (
    .in0(out_17), .in1(out_16), .in2(out_18), .in3(in_4), .out(multiplexer_3_out), .sel(in_1), .en(in_13));
  D_Flip_Flop d_ff_3 (.clk(clock_1_out), .D(multiplexer_3_out), .Q(out_17), .reset(in_12));  // open: Qn, preset, en
  D_Flip_Flop d_ff_4 (.clk(clock_1_out), .D(multiplexer_4_out), .Q(out_18), .reset(in_12));  // open: Qn, preset, en
  Multiplexer #(.select(2)) multiplexer_4 (
    .in0(out_18), .in1(out_17), .in2(out_19), .in3(in_5), .out(multiplexer_4_out), .sel(in_1), .en(in_13));
  Multiplexer #(.select(2)) multiplexer_5 (
    .in0(out_19), .in1(out_18), .in2(out_20), .in3(in_6), .out(multiplexer_5_out), .sel(in_1), .en(in_13));
  D_Flip_Flop d_ff_5 (.clk(clock_1_out), .D(multiplexer_5_out), .Q(out_19), .reset(in_12));  // open: Qn, preset, en
  D_Flip_Flop d_ff_6 (.clk(clock_1_out), .D(multiplexer_6_out), .Q(out_20), .reset(in_12));  // open: Qn, preset, en
  Multiplexer #(.select(2)) multiplexer_6 (
    .in0(out_20), .in1(out_19), .in2(out_21), .in3(in_7), .out(multiplexer_6_out), .sel(in_1), .en(in_13));
  D_Flip_Flop d_ff_7 (.clk(clock_1_out), .D(multiplexer_7_out), .Q(out_21), .reset(in_12));  // open: Qn, preset, en
  Multiplexer #(.select(2)) multiplexer_7 (
    .in0(out_21), .in1(out_20), .in2(out_14), .in3(in_8), .out(multiplexer_7_out), .sel(in_1), .en(in_13));
  Multiplexer #(.select(2)) multiplexer_8 (
    .in0(out_14), .in1(out_21), .in2(in_2), .in3(in_9), .out(multiplexer_8_out), .sel(in_1), .en(in_13));
  D_Flip_Flop d_ff_8 (.clk(clock_1_out), .D(multiplexer_8_out), .Q(out_14), .reset(in_12));  // open: Qn, preset, en
endmodule

module SIPO (
  input  in_1,
  input  in_2,
  input  in_3,
  input  in_4,
  input  in_5,
  input  in_6,
  input  in_7,
  input  in_8,
  input  clear,
  output out_10,
  output out_11,
  output out_12,
  output out_13,
  output out_14,
  output out_15,
  output out_16,
  output out_17
);

  wire clock_1_out;

  Clock clock_1 (.out(clock_1_out));
  D_Flip_Flop d_ff_1 (.clk(clock_1_out), .D(in_1), .Q(out_10), .reset(clear));  // open: Qn, preset, en
  D_Flip_Flop d_ff_2 (.clk(clock_1_out), .D(in_2), .Q(out_11), .reset(clear));  // open: Qn, preset, en
  D_Flip_Flop d_ff_3 (.clk(clock_1_out), .D(in_3), .Q(out_12), .reset(clear));  // open: Qn, preset, en
  D_Flip_Flop d_ff_4 (.clk(clock_1_out), .D(in_4), .Q(out_13), .reset(clear));  // open: Qn, preset, en
  D_Flip_Flop d_ff_5 (.clk(clock_1_out), .D(in_5), .Q(out_14), .reset(clear));  // open: Qn, preset, en
  D_Flip_Flop d_ff_6 (.clk(clock_1_out), .D(in_6), .Q(out_15), .reset(clear));  // open: Qn, preset, en
  D_Flip_Flop d_ff_7 (.clk(clock_1_out), .D(in_7), .Q(out_16), .reset(clear));  // open: Qn, preset, en
  D_Flip_Flop d_ff_8 (.clk(clock_1_out), .D(in_8), .Q(out_17), .reset(clear));  // open: Qn, preset, en
endmodule
