// Logisim project PIPO.crt.circ as structural Verilog: 3 circuits, main circuit main
module main (
  input  in_1,
  input  enable,
  input  clock,
  input  in_4,
  input  [7:0] in_5,
  input  in_6,
  input  [7:0] in_7,
  input  in_8,
  input  [7:0] in_9,
  input  [7:0] in_10,
  input  in_11,
  input  in_12,
  input  [7:0] in_13,
  input  [7:0] in_14,
  input  in_15,
  input  in_16,
  input  [2:0] in_17,
  input  [2:0] in_18,
  input  [7:0] in_19,
  input  [7:0] in_20,
  input  in_21,
  input  in_22,
  output [7:0] out_23,
  output [7:0] out_24,
  output [7:0] out_25,
  output [7:0] out_26,
  output [7:0] out_27,
  output [7:0] out_28,
  output [7:0] out_29,
  output [7:0] out_30,
  output [7:0] out_31,
  output [7:0] out_32,
  output [7:0] out_33,
  output [7:0] out_34,
  output [7:0] out_35,
  output [7:0] out_36
);

  wire [7:0] demultiplexer_1_out2, demultiplexer_1_out3, demultiplexer_1_out4, demultiplexer_1_out5,
       demultiplexer_1_out6, demultiplexer_1_out7, multiplexer_1_out, multiplexer_2_out, multiplexer_3_out,
       multiplexer_6_out, multiplexer_7_out, multiplexer_8_out, multiplexer_9_out;

  Multiplexer #(.width(8)) multiplexer_1 (
    .in0(demultiplexer_1_out2), .in1(in_13), .out(multiplexer_1_out), .sel(in_15));  // open: en
  Multiplexer #(.width(8)) multiplexer_2 (
    .in0(demultiplexer_1_out3), .in1(in_19), .out(multiplexer_2_out), .sel(in_21));  // open: en
  Multiplexer #(.width(8)) multiplexer_3 (.in0(out_26), .in1(in_5), .out(multiplexer_3_out), .sel(in_6));  // open: en
  Multiplexer #(.width(8)) multiplexer_4 (.in0(out_29), .in1(in_9), .out(out_30), .sel(in_11));  // open: en
  PIPO_trial pipo_trial_1 (
    .clock(in_1), .enable(enable), .\input (multiplexer_3_out), .\output (out_23));  // open: preset, clear
  PIPO_trial pipo_trial_2 (.clock(in_1), .enable(enable), .\input (out_30), .\output (out_27));  // open: preset, clear
  PIPO_trial pipo_trial_3 (
    .clock(in_1), .enable(enable), .\input (multiplexer_1_out), .\output (out_31));  // open: preset, clear
  PIPO_trial pipo_trial_4 (
    .clock(in_1), .enable(enable), .\input (multiplexer_2_out), .\output (out_35));  // open: preset, clear
  Multiplexer #(.select(3), .width(8)) multiplexer_5 (
    .in0(out_23), .in1(out_27), .in2(out_31), .in3(out_35), .in4(out_25), .in5(out_28), .in6(out_33),
    .in7(out_36), .out(out_34), .sel(in_18), .en(1'b1));
  Demultiplexer #(.select(3), .width(8)) demultiplexer_1 (
    .out0(out_26), .out1(out_29), .out2(demultiplexer_1_out2), .out3(demultiplexer_1_out3),
    .out4(demultiplexer_1_out4), .out5(demultiplexer_1_out5), .out6(demultiplexer_1_out6),
    .out7(demultiplexer_1_out7), .in(out_34), .sel(in_17), .en(1'b1));
  Multiplexer #(.width(8)) multiplexer_6 (
    .in0(demultiplexer_1_out4), .in1(in_7), .out(multiplexer_6_out), .sel(in_8));  // open: en
  Multiplexer #(.width(8)) multiplexer_7 (
    .in0(demultiplexer_1_out5), .in1(in_10), .out(multiplexer_7_out), .sel(in_12));  // open: en
  Multiplexer #(.width(8)) multiplexer_8 (
    .in0(demultiplexer_1_out6), .in1(in_14), .out(multiplexer_8_out), .sel(in_16));  // open: en
  Multiplexer #(.width(8)) multiplexer_9 (
    .in0(demultiplexer_1_out7), .in1(in_20), .out(multiplexer_9_out), .sel(in_22));  // open: en
  PIPO_trial pipo_trial_5 (
    .clock(clock), .enable(in_4), .\input (multiplexer_6_out), .\output (out_25));  // open: preset, clear
  PIPO_trial pipo_trial_6 (
    .clock(clock), .enable(in_4), .\input (multiplexer_7_out), .\output (out_28));  // open: preset, clear
  PIPO_trial pipo_trial_7 (
    .clock(clock), .enable(in_4), .\input (multiplexer_8_out), .\output (out_33));  // open: preset, clear
  PIPO_trial REG_7 (
    .clock(clock), .enable(in_4), .\input (multiplexer_9_out), .\output (out_36));  // open: preset, clear

  assign out_24 = out_23;
  assign out_32 = out_29;
endmodule

module PIPO (
  input  clock,
  input  in_1,
  input  in_3,
  input  in_4,
  input  in_4_2,
  input  in_5,
  input  in_7,
  input  in_8,
  input  in_8_2,
  input  preset,
  input  enable,
  input  clear,
  output out_8,
  output out_4,
  output out_5,
  output out_16,
  output out_1,
  output out_18,
  output out_19,
  output out_20
);

  D_Flip_Flop d_ff_1 (.clk(clock), .D(in_1), .Q(out_1), .preset(preset), .en(enable), .reset(clear));  // open: Qn
  D_Flip_Flop d_ff_2 (.clk(clock), .D(in_3), .Q(out_18), .preset(preset), .en(enable));  // open: Qn, reset
  D_Flip_Flop d_ff_3 (.clk(clock), .D(in_4), .Q(out_19), .preset(preset), .en(enable));  // open: Qn, reset
  D_Flip_Flop d_ff_4 (.clk(clock), .D(in_4_2), .Q(out_4), .preset(preset), .en(enable), .reset(clear));  // open: Qn
  D_Flip_Flop d_ff_5 (.clk(clock), .D(in_5), .Q(out_5), .preset(preset), .en(enable), .reset(clear));  // open: Qn
  D_Flip_Flop d_ff_6 (.clk(clock), .D(in_7), .Q(out_20), .preset(preset), .en(enable));  // open: Qn, reset
  D_Flip_Flop d_ff_7 (.clk(clock), .D(in_8), .Q(out_16), .preset(preset), .en(enable));  // open: Qn, reset
  D_Flip_Flop d_ff_8 (.clk(clock), .D(in_8_2), .Q(out_8), .preset(preset), .en(enable), .reset(clear));  // open: Qn
endmodule

module PIPO_trial (
  input  clock,
  input  preset,
  input  enable,
  input  clear,
  input  [7:0] \input ,
  output [7:0] \output 
);

  D_Flip_Flop d_ff_1 (
    .clk(clock), .D(\input [0]), .Q(\output [0]), .preset(preset), .en(enable), .reset(clear));  // open: Qn
  D_Flip_Flop d_ff_2 (.clk(clock), .D(\input [1]), .Q(\output [1]), .preset(preset), .en(enable));  // open: Qn, reset
  D_Flip_Flop d_ff_3 (.clk(clock), .D(\input [2]), .Q(\output [2]), .preset(preset), .en(enable));  // open: Qn, reset
  D_Flip_Flop d_ff_4 (
    .clk(clock), .D(\input [3]), .Q(\output [3]), .preset(preset), .en(enable), .reset(clear));  // open: Qn
  D_Flip_Flop d_ff_5 (
    .clk(clock), .D(\input [4]), .Q(\output [4]), .preset(preset), .en(enable), .reset(clear));  // open: Qn
  D_Flip_Flop d_ff_6 (.clk(clock), .D(\input [5]), .Q(\output [5]), .preset(preset), .en(enable));  // open: Qn, reset
  D_Flip_Flop d_ff_7 (.clk(clock), .D(\input [6]), .Q(\output [6]), .preset(preset), .en(enable));  // open: Qn, reset
  D_Flip_Flop d_ff_8 (
    .clk(clock), .D(\input [7]), .Q(\output [7]), .preset(preset), .en(enable), .reset(clear));  // open: Qn
endmodule
