// Logisim project PISO.circ as structural Verilog
module PISO (
  input  IN_0,
  input  IN_1,
  input  IN_2,
  input  IN_3,
  input  IN_4,
  input  IN_5,
  input  IN_6,
  input  IN_7,
  input  clear,
  output out_10,
  output out_11,
  output out_12,
  output out_13,
  output out_14,
  output out_15,
  output out_16,
  output out_17
);

  wire clock_1_out;

  Clock clock_1 (.out(clock_1_out));
  D_Flip_Flop d_ff_1 (.clk(clock_1_out), .D(IN_0), .Q(out_10), .reset(clear));  // open: Qn, preset, en
  D_Flip_Flop d_ff_2 (.clk(clock_1_out), .D(IN_1), .Q(out_11), .reset(clear));  // open: Qn, preset, en
  D_Flip_Flop d_ff_3 (.clk(clock_1_out), .D(IN_2), .Q(out_12), .reset(clear));  // open: Qn, preset, en
  D_Flip_Flop d_ff_4 (.clk(clock_1_out), .D(IN_3), .Q(out_13), .reset(clear));  // open: Qn, preset, en
  D_Flip_Flop d_ff_5 (.clk(clock_1_out), .D(IN_4), .Q(out_14), .reset(clear));  // open: Qn, preset, en
  D_Flip_Flop d_ff_6 (.clk(clock_1_out), .D(IN_5), .Q(out_15), .reset(clear));  // open: Qn, preset, en
  D_Flip_Flop d_ff_7 (.clk(clock_1_out), .D(IN_6), .Q(out_16), .reset(clear));  // open: Qn, preset, en
  D_Flip_Flop d_ff_8 (.clk(clock_1_out), .D(IN_7), .Q(out_17), .reset(clear));  // open: Qn, preset, en
endmodule
